// Logisim project 123.circ as structural Verilog: 1 circuit, main circuit main
module main (
  input  a,
  input  b,
  output x,
  output y,
  output z,
  output u
);

  wire not_1_out, not_2_out, not_3_out, not_4_out;

  not not_1 (not_1_out, a);
  not not_2 (not_2_out, b);
  not not_3 (not_3_out, b);
  not not_4 (not_4_out, a);
  and and_1 (u, b, a);
  and and_2 (x, not_1_out, not_2_out);
  and and_3 (y, not_3_out, a);
  and and_4 (z, b, not_4_out);
endmodule
