// Logisim project 1.circ as structural Verilog: 1 circuit, main circuit main
module main (
  input  in_1
);

  // AND_Gate and_1 has open pins: out=in_1

  // Notes on the sheet:
  //   wwwww
endmodule
